// Logisim project cpu.circ as structural Verilog: 13 circuits, main circuit main
module main (
  input  [31:0] INSTRUCTION,
  input  CLOCK,
  output [31:0] FETCH_ADDRESS,
  output [31:0] ra,
  output [31:0] sp,
  output [31:0] t0,
  output [31:0] t1,
  output [31:0] t2,
  output [31:0] s0,
  output [31:0] s1,
  output [31:0] a0
);

  wire a_selector_1_asel, b_selector_1_bsel, BrEq, BrLt, BrUn, memrw_1_memrw, PCSel, reg_w_en_sel_1_regwen;
  wire [1:0] wb_sel_1_wbsel;
  wire [3:0] ALUSel;
  wire [4:0] ImmSel, register_retreiver_1_rd, register_retreiver_1_rs1, register_retreiver_1_rs2;
  wire [31:0] adder_1_out, ALUA, ALUB, ALUResult, DataA, DataB, DataR, imm_gen_1_immediate, instr_new,
       multiplexer_1_out, multiplexer_2_out, pc_new, PC_plus_IV, wb;

  Adder #(.width(32)) adder_1 (.a(PC_plus_IV), .b(32'h4), .out(adder_1_out));  // open: cin, cout
  Register #(.width(32)) PC (.D(multiplexer_1_out), .clk(CLOCK), .Q(PC_plus_IV));  // open: en, clr
  Multiplexer #(.width(32), .enable("false")) multiplexer_1 (
    .in0(adder_1_out), .in1(ALUResult), .out(multiplexer_1_out), .sel(PCSel));
  Shifter #(.width(32), .shift("lr")) shifter_1 (.in(PC_plus_IV), .\dist (5'b00010), .out(FETCH_ADDRESS));
  register_retreiver register_retreiver_1 (
    .Instruction(instr_new), .RS1(register_retreiver_1_rs1), .RS2(register_retreiver_1_rs2),
    .RD(register_retreiver_1_rd));
  reg_w_en_sel reg_w_en_sel_1 (.ImmSel(ImmSel), .RegWEn(reg_w_en_sel_1_regwen));
  pc_selector pc_selector_1 (
    .Instruction(instr_new), .ImmSel(ImmSel), .BrEq(BrEq), .BrLt(BrLt), .PCSel(PCSel), .BrUn(BrUn));
  regfile_main RegFile (
    .rs2(register_retreiver_1_rs2), .rd(register_retreiver_1_rd), .Read_Data_1(DataA), .Read_Data_2(DataB),
    .ra(ra), .sp(sp), .t0(t0), .t1(t1), .t2(t2), .s0(s0), .s1(s1), .a0(a0), .rs1(register_retreiver_1_rs1),
    .Write_Data(wb), .RegWEn(reg_w_en_sel_1_regwen), .clk(CLOCK));
  Register #(.width(32)) register_1 (.D(PC_plus_IV), .clk(CLOCK), .Q(pc_new));  // open: en, clr
  Multiplexer #(.width(32), .enable("false")) multiplexer_2 (
    .in0(INSTRUCTION), .in1(32'h13), .out(multiplexer_2_out), .sel(PCSel));
  Register #(.width(32)) register_2 (.D(multiplexer_2_out), .clk(CLOCK), .Q(instr_new));  // open: en, clr
  imm_sel_gen imm_sel_gen_1 (.Instruction(instr_new), .ImmSel(ImmSel));
  imm_gen imm_gen_1 (.Instruction(instr_new), .ImmSel(ImmSel), .Immediate(imm_gen_1_immediate));
  Multiplexer #(.width(32), .enable("false")) multiplexer_3 (
    .in0(DataB), .in1(imm_gen_1_immediate), .out(ALUB), .sel(b_selector_1_bsel));
  b_selector b_selector_1 (.ImmSel(ImmSel), .BSel(b_selector_1_bsel));
  a_selector a_selector_1 (.ImmSel(ImmSel), .ASel(a_selector_1_asel));
  branch_comp branch_comp_1 (.DataA(DataA), .DataB(DataB), .BrUn(BrUn), .BrEq(BrEq), .BrLT(BrLt));
  Multiplexer #(.width(32), .enable("false")) multiplexer_4 (
    .in0(DataA), .in1(pc_new), .out(ALUA), .sel(a_selector_1_asel));
  alu_sel_sel alu_sel_sel_1 (.ImmSel(ImmSel), .Instruction(instr_new), .ALUSel(ALUSel));
  alu Arithmetic_Logic_Unit (.A(ALUA), .B(ALUB), .ALUSel(ALUSel), .Result(ALUResult));
  MemRW memrw_1 (.ImmSel(ImmSel), .MemRW(memrw_1_memrw));
  // mem_main DMEM: pin names not known; wires that end beside it: ALUResult, DataB, memrw_1_memrw, CLOCK, DataR
  write_bit write_bit_1 (.two(PC_plus_IV), .one(ALUResult), .zero(DataR), .WBSel(wb_sel_1_wbsel), .wb(wb));
  wb_sel wb_sel_1 (.ImmSel(ImmSel), .WBSel(wb_sel_1_wbsel));

  // Other names for the same wires on the sheet: clk = CLOCK; PROGRAM_COUNTER[31:0] = PC_plus_IV

  // Notes on the sheet:
  //   Output
  //   Inputs/Outputs from run.circ. DO NOT MOVE THESE.
  //   Inputs
  //   Inputs/Outputs from run.circ. DO NOT MOVE THESE.
endmodule

module alu_sel_sel (
  input  [4:0] ImmSel,
  input  [31:0] Instruction,
  output [3:0] ALUSel
);

  wire and_1_out, comparator_1_eq, comparator_2_eq, comparator_3_eq, comparator_4_eq, comparator_5_eq,
       comparator_6_eq, comparator_7_eq, comparator_8_eq, comparator_9_eq, comparator_10_eq, or_1_out,
       or_2_out;
  wire [1:0] multiplexer_1_out;
  wire [4:0] multiplexer_2_out;

  Comparator #(.width(5)) comparator_1 (.a(5'b00100), .b(ImmSel), .eq(comparator_1_eq));  // open: gt, lt
  Comparator #(.width(3)) comparator_2 (.a(3'b000), .b(Instruction[14:12]), .eq(comparator_2_eq));  // open: gt, lt
  Comparator #(.width(3)) comparator_3 (.a(3'b010), .b(Instruction[14:12]), .eq(comparator_3_eq));  // open: gt, lt
  Comparator #(.width(3)) comparator_4 (.a(3'b100), .b(Instruction[14:12]), .eq(comparator_4_eq));  // open: gt, lt
  Comparator #(.width(3)) comparator_5 (.a(3'b110), .b(Instruction[14:12]), .eq(comparator_5_eq));  // open: gt, lt
  Comparator #(.width(3)) comparator_6 (.a(3'b111), .b(Instruction[14:12]), .eq(comparator_6_eq));  // open: gt, lt
  or or_1 (or_1_out, comparator_2_eq, comparator_3_eq, comparator_4_eq, comparator_5_eq, comparator_6_eq);
  Comparator #(.width(5)) comparator_7 (.a(ImmSel), .b(5'b11001), .eq(comparator_7_eq));  // open: gt, lt
  Comparator #(.width(5)) comparator_8 (.a(ImmSel), .b({5{1'b0}}), .eq(comparator_8_eq));  // open: gt, lt
  Comparator #(.width(5)) comparator_9 (.a(ImmSel), .b(5'b00100), .eq(comparator_9_eq));  // open: gt, lt
  Comparator #(.width(5)) comparator_10 (.a(ImmSel), .b(5'b01100), .eq(comparator_10_eq));  // open: gt, lt
  and and_1 (and_1_out, or_1_out, comparator_1_eq);
  Multiplexer #(.width(2), .enable("false")) multiplexer_1 (
    .in0({Instruction[30], Instruction[25]}), .in1(2'b00), .out(multiplexer_1_out), .sel(and_1_out));
  or or_2 (or_2_out, comparator_7_eq, comparator_8_eq, comparator_9_eq, comparator_10_eq);
  Multiplexer #(.width(5), .enable("false")) multiplexer_2 (
    .in0({5{1'b0}}), .in1({multiplexer_1_out, Instruction[14:12]}), .out(multiplexer_2_out), .sel(or_2_out));
  Multiplexer #(.select(5), .width(4), .enable("false")) multiplexer_3 (
    .in0(4'b0000), .in1(4'b0110), .in2(4'b0111), .in4(4'b0011), .in5(4'b0100), .in6(4'b0010), .in7(4'b0001),
    .in8(4'b1010), .in9(4'b1110), .in11(4'b1011), .in13(4'b1000), .in15(4'b1001), .in16(4'b1100),
    .in21(4'b0101), .out(ALUSel), .sel(multiplexer_2_out));  // open: in3, in10, in12, in14, in17, in18, in19, in20, in22, in23, in24, in25, in26, in27, in28, in29, in30, in31
endmodule

module imm_gen (
  input  [31:0] Instruction,
  input  [4:0] ImmSel,
  output [31:0] Immediate
);

  wire [11:0] bit_extender_4_out;
  wire [19:0] bit_extender_3_out;
  wire [20:0] bit_extender_1_out, bit_extender_2_out;

  assign bit_extender_1_out = {{20{Instruction[31]}}, Instruction[31]};  // Bit_Extender bit_extender_1
  assign bit_extender_2_out = {{20{Instruction[31]}}, Instruction[31]};  // Bit_Extender bit_extender_2
  assign bit_extender_3_out = {{19{Instruction[31]}}, Instruction[31]};  // Bit_Extender bit_extender_3
  assign bit_extender_4_out = {{11{Instruction[31]}}, Instruction[31]};  // Bit_Extender bit_extender_4
  Multiplexer #(.select(5), .width(32), .enable("false")) multiplexer_1 (
    .in0({bit_extender_1_out, Instruction[30:20]}), .in4({bit_extender_1_out, Instruction[30:20]}),
    .in5({Instruction[31:12], {12{1'b0}}}),
    .in8({bit_extender_2_out, Instruction[30:25], Instruction[11:7]}),
    .in13({Instruction[31:12], {12{1'b0}}}),
    .in24({bit_extender_3_out, Instruction[7], Instruction[30:25], Instruction[11:8], 1'b0}),
    .in25({bit_extender_1_out, Instruction[30:20]}),
    .in27({bit_extender_4_out, Instruction[19:12], Instruction[20], Instruction[30:21], 1'b0}),
    .out(Immediate), .sel(ImmSel));  // open: in1, in2, in3, in6, in7, in9, in10, in11, in12, in14, in15, in16, in17, in18, in19, in20, in21, in22, in23, in26, in28, in29, in30, in31

  // Notes on the sheet:
  //   I
  //   S
  //   B
  //   J
  //   U
endmodule

module write_bit (
  input  [31:0] two,
  input  [31:0] one,
  input  [31:0] zero,
  input  [1:0] WBSel,
  output [31:0] wb
);

  Multiplexer #(.select(2), .width(32), .enable("false")) multiplexer_1 (
    .in0(zero), .in1(one), .in2(two), .out(wb), .sel(WBSel));  // open: in3
endmodule

module imm_sel_gen (
  input  [31:0] Instruction,
  output [4:0] ImmSel
);


  assign ImmSel = Instruction[6:2];
endmodule

module b_selector (
  input  [4:0] ImmSel,
  output BSel
);

  Multiplexer #(.select(5), .enable("false")) multiplexer_1 (
    .in0(1'b1), .in4(1'b1), .in5(1'b1), .in8(1'b1), .in12(1'b0), .in13(1'b1), .in24(1'b1), .in25(1'b1),
    .in27(1'b1), .out(BSel), .sel(ImmSel));  // open: in1, in2, in3, in6, in7, in9, in10, in11, in14, in15, in16, in17, in18, in19, in20, in21, in22, in23, in26, in28, in29, in30, in31
endmodule

module a_selector (
  input  [4:0] ImmSel,
  output ASel
);

  Multiplexer #(.select(5), .enable("false")) multiplexer_1 (
    .in0(1'b0), .in4(1'b0), .in5(1'b1), .in8(1'b0), .in12(1'b0), .in13(1'b0), .in24(1'b1), .in25(1'b0),
    .in27(1'b1), .out(ASel), .sel(ImmSel));  // open: in1, in2, in3, in6, in7, in9, in10, in11, in14, in15, in16, in17, in18, in19, in20, in21, in22, in23, in26, in28, in29, in30, in31
endmodule

module register_retreiver (
  input  [31:0] Instruction,
  output [4:0] RS1,
  output [4:0] RS2,
  output [4:0] RD
);


  assign RD = Instruction[11:7];
  assign RS1 = Instruction[19:15];
  assign RS2 = Instruction[24:20];
endmodule

module branch_comp (
  input  [31:0] DataA,
  input  [31:0] DataB,
  input  BrUn,
  output BrEq,
  output BrLT
);

  wire comparator_1_eq, comparator_1_lt, comparator_2_eq, comparator_2_lt;

  Comparator #(.width(32)) comparator_1 (.a(DataA), .b(DataB), .eq(comparator_1_eq), .lt(comparator_1_lt));  // open: gt
  Comparator #(.width(32), .mode("unsigned")) comparator_2 (
    .a(DataA), .b(DataB), .eq(comparator_2_eq), .lt(comparator_2_lt));  // open: gt
  Multiplexer #(.enable("false")) multiplexer_1 (.in0(comparator_1_eq), .in1(comparator_2_eq), .out(BrEq), .sel(BrUn));
  Multiplexer #(.enable("false")) multiplexer_2 (.in0(comparator_1_lt), .in1(comparator_2_lt), .out(BrLT), .sel(BrUn));
endmodule

module pc_selector (
  input  [31:0] Instruction,
  input  [4:0] ImmSel,
  input  BrEq,
  input  BrLt,
  output PCSel,
  output BrUn
);

  wire and_2_out, and_3_out, and_4_out, comparator_1_eq, comparator_2_eq, comparator_3_eq, comparator_4_eq,
       not_1_out, not_2_out;

  and and_1 (BrUn, Instruction[13], comparator_2_eq);
  Comparator #(.width(5)) comparator_1 (.a(5'b11011), .b(ImmSel), .eq(comparator_1_eq));  // open: gt, lt
  Comparator #(.width(5)) comparator_2 (.a(ImmSel), .b(5'b11000), .eq(comparator_2_eq));  // open: gt, lt
  and and_2 (and_2_out, comparator_2_eq, BrLt);
  Comparator #(.width(5)) comparator_3 (.a(5'b11000), .b(ImmSel), .eq(comparator_3_eq));  // open: gt, lt
  not not_1 (not_1_out, Instruction[12]);
  and and_3 (and_3_out, comparator_3_eq, BrEq, not_1_out);
  or or_1 (PCSel, comparator_1_eq, and_3_out, and_2_out, and_4_out, comparator_4_eq);
  Comparator #(.width(5)) comparator_4 (.a(5'b11001), .b(ImmSel), .eq(comparator_4_eq));  // open: gt, lt
  not not_2 (not_2_out, BrEq);
  and and_4 (and_4_out, Instruction[12], comparator_3_eq, not_2_out);
endmodule

module MemRW (
  input  [4:0] ImmSel,
  output MemRW
);

  Comparator #(.width(5)) comparator_1 (.a(5'b01000), .b(ImmSel), .eq(MemRW));  // open: gt, lt
endmodule

module reg_w_en_sel (
  input  [4:0] ImmSel,
  output RegWEn
);

  Multiplexer #(.select(5), .enable("false")) multiplexer_1 (
    .in0(1'b1), .in4(1'b1), .in5(1'b1), .in12(1'b1), .in13(1'b1), .in25(1'b1), .in27(1'b1), .out(RegWEn),
    .sel(ImmSel));  // open: in1, in2, in3, in6, in7, in8, in9, in10, in11, in14, in15, in16, in17, in18, in19, in20, in21, in22, in23, in24, in26, in28, in29, in30, in31
endmodule

module wb_sel (
  input  [4:0] ImmSel,
  output [1:0] WBSel
);

  Multiplexer #(.select(5), .width(2), .enable("false")) multiplexer_1 (
    .in0(2'b00), .in4(2'b01), .in5(2'b01), .in12(2'b01), .in13(2'b01), .in25(2'b10), .in27(2'b10),
    .out(WBSel), .sel(ImmSel));  // open: in1, in2, in3, in6, in7, in8, in9, in10, in11, in14, in15, in16, in17, in18, in19, in20, in21, in22, in23, in24, in26, in28, in29, in30, in31
endmodule
